// Logisim project 3.1_Comp4.circ as structural Verilog: 4 circuits, main circuit main
module main (
);

  Comp1bit comp1bit_1 ();  // open: a, b, Cin, Cout
  Comp4nat comp4nat_1 ();  // open: A_B, A_B_2, A_B_3, A, B
  Comp4ent comp4ent_1 ();  // open: A_B, A_B_2, A_B_3, A, B
endmodule

module Comp1bit (
  input  a,
  input  b,
  input  [2:0] Cin,
  output [2:0] Cout
);
endmodule

module Comp4nat (
  input  [3:0] A,
  input  [3:0] B,
  output A_B,
  output A_B_2,
  output A_B_3
);

  wire [2:0] bit0_cout, bit1_cout, bit2_cout, bit3_cout, undriven;

  Comp1bit bit3 (.a(A[3]), .b(B[3]), .Cin(bit2_cout), .Cout(bit3_cout));
  Comp1bit bit2 (.a(A[2]), .b(B[2]), .Cin(bit1_cout), .Cout(bit2_cout));
  Comp1bit bit1 (.a(A[1]), .b(B[1]), .Cin(bit0_cout), .Cout(bit1_cout));
  Comp1bit bit0 (.a(A[0]), .b(B[0]), .Cin(undriven), .Cout(bit0_cout));
endmodule

module Comp4ent (
  input  [3:0] A,
  input  [3:0] B,
  output A_B,
  output A_B_2,
  output A_B_3
);

  wire [2:0] bit0_cout, bit1_cout, bit2_cout, bit3_cout, undriven;

  Comp1bit bit3 (.Cin(bit2_cout), .Cout(bit3_cout));  // open: a, b
  Comp1bit bit2 (.a(A[2]), .b(B[2]), .Cin(bit1_cout), .Cout(bit2_cout));
  Comp1bit bit1 (.a(A[1]), .b(B[1]), .Cin(bit0_cout), .Cout(bit1_cout));
  Comp1bit bit0 (.a(A[0]), .b(B[0]), .Cin(undriven), .Cout(bit0_cout));

  // Notes on the sheet:
  //   Sa
  //   Sb
endmodule
