// Logisim project BancRegsBiport+PC.circ as structural Verilog: 4 circuits, main circuit main
module main (
  input  Load,
  input  Increment,
  input  in_3
);

  wire button_1_out, button_2_out, Reset_out, Sincro_out;
  wire [1:0] slider_2_out, slider_3_out, slider_4_out;
  wire [7:0] bancregistres4x8b_1_regout1, bancregistres4x8b_1_regout2, New_PC_value_out, pc8bits_1_pcout,
       slider_1_out;

  Button Sincro (.out(Sincro_out));
  Slider #(.value('hfb)) New_PC_value (.out(New_PC_value_out));
  PC8bits pc8bits_1 (
    .NewPC(New_PC_value_out), .Load(Load), .Inc(Increment), .Sinc(Sincro_out), .Reset(Reset_out),
    .PCout(pc8bits_1_pcout));
  // Probe on pc8bits_1_pcout
  Button Reset (.out(Reset_out));
  Slider #(.value('h54)) slider_1 (.out(slider_1_out));
  Slider #(.width(2), .value('h3)) slider_2 (.out(slider_2_out));
  Slider #(.width(2), .value('h2)) slider_3 (.out(slider_3_out));
  Slider #(.width(2), .value('h1)) slider_4 (.out(slider_4_out));
  Button button_1 (.out(button_1_out));
  Button button_2 (.out(button_2_out));
  BancRegistres4x8b bancregistres4x8b_1 (
    .RegIn(slider_1_out), .\NúmRegIn (slider_2_out), .Wr(in_3), .Sinc(button_1_out), .Reset(button_2_out),
    .RegOut1(bancregistres4x8b_1_regout1), .RegOut2(bancregistres4x8b_1_regout2),
    .\NúmRegOut1 (slider_3_out), .\NúmRegOut2 (bancregistres4x8b_1_regout2[1:0]));
  // Probe on bancregistres4x8b_1_regout2
  // Probe on bancregistres4x8b_1_regout1
  // Pins of 2 and 8 bits meet at bancregistres4x8b_1_regout2
endmodule

module BancRegistres4x8b (
  input  [7:0] RegIn,
  input  [1:0] \NúmRegIn ,
  input  Wr,
  input  Sinc,
  input  Reset,
  input  [1:0] \NúmRegOut1 ,
  input  [1:0] \NúmRegOut2 ,
  output [7:0] RegOut1,
  output [7:0] RegOut2
);

  wire demultiplexer_1_out0, demultiplexer_1_out1, demultiplexer_1_out2;
  wire [7:0] R0_dout, R1_dout, R2_dout, R3_dout;

  Demultiplexer #(.select(2), .enable("false")) demultiplexer_1 (
    .out0(demultiplexer_1_out0), .out1(demultiplexer_1_out1), .out2(demultiplexer_1_out2),
    .out3(demultiplexer_1_out2), .in(Wr), .sel(\NúmRegIn ));
  Multiplexer #(.select(2), .width(8), .enable("false")) multiplexer_1 (
    .in0(R0_dout), .in1(R1_dout), .in2(R2_dout), .in3(R3_dout), .out(RegOut1), .sel(\NúmRegOut1 ));
  Multiplexer #(.select(2), .width(8), .enable("false")) multiplexer_2 (
    .in0(R0_dout), .in1(R1_dout), .in2(R2_dout), .in3(R3_dout), .out(RegOut2), .sel(\NúmRegOut2 ));
  Registre8bits R0 (.Wr(demultiplexer_1_out0), .Sinc(Sinc), .Reset(Reset), .Din(RegIn), .Dout(R0_dout));
  Registre8bits R1 (.Wr(demultiplexer_1_out1), .Sinc(Sinc), .Reset(Reset), .Din(RegIn), .Dout(R1_dout));
  Registre8bits R2 (.Wr(demultiplexer_1_out2), .Sinc(Sinc), .Reset(Reset), .Din(RegIn), .Dout(R2_dout));
  Registre8bits R3 (.Wr(demultiplexer_1_out2), .Sinc(Sinc), .Reset(Reset), .Din(RegIn), .Dout(R3_dout));
endmodule

module PC8bits (
  input  [7:0] NewPC,
  input  Load,
  input  Inc,
  input  Sinc,
  input  Reset,
  output [7:0] PCout
);

  wire or_1_out;
  wire [7:0] adder_1_out, multiplexer_1_out;

  or or_1 (or_1_out, Load, Inc);
  Multiplexer #(.width(8), .enable("false")) multiplexer_1 (
    .in0(adder_1_out), .in1(NewPC), .out(multiplexer_1_out), .sel(Load));
  Registre8bits registre8bits_1 (.Wr(or_1_out), .Sinc(Sinc), .Reset(Reset), .Din(multiplexer_1_out), .Dout(PCout));
  Adder adder_1 (.a(8'h1), .b(PCout), .out(adder_1_out));  // open: cin, cout

  // Notes on the sheet:
  //   INCREMENTEM
endmodule

module Registre8bits (
  input  [7:0] Din,
  input  Wr,
  input  Sinc,
  input  Reset,
  output [7:0] Dout
);

  Register #(.Select("low")) Reg8b (.D(Din), .en(Wr), .Q(Dout), .clk(Sinc), .clr(Reset));
endmodule
